# Fritzing sketch LEDGame_Sketch (saved by Fritzing 0.9.5d)

parts:
  Компонент1 = Arduino Uno (Rev3) - ICSP
  VCC2 = Battery block 9V
  S1 = Toggle Switch [package=THT]
  LCD1 = LCD screen
  LCM1602_IIC1 = LCM1602 IIC [part_number="LCM1602 IIC" chip_label="LCM1602 IIC" package="DIP (Dual Inline) [THT]"]
  DC-DC_5V_to_3V3 = KA78R05 Low Dropout Voltage Regulator [part_number=KA78R05 package=TO-220F-4L]
  SG4 = Piezo [package=buzzer-12mm-ns-kit]
  S6 = Pushbutton [package="[SMD]"]
  S7 = Pushbutton [package="[SMD]"]
  S8 = Pushbutton [package="[SMD]"]
  LED1 = smd LED [color="Green (565nm)" package="1206 [SMD]"]
  LED2 = smd LED [color="Yellow (595nm)" package="1206 [SMD]"]
  LED3 = smd LED [color="Red (633nm)" package="1206 [SMD]"]
  R1 = Resistor [tolerance=±5% resistance=150 package="2512 [SMD]"]
  R1-3 = Resistor [tolerance=±5% resistance=150 package="2512 [SMD]"]
  R3 = Resistor [tolerance=±5% resistance=150 package="2512 [SMD]"]
  DC-DC_5V_to_3V3_2 = KA78R05 Low Dropout Voltage Regulator [part_number=KA78R05 package=TO-220F-4L]
  R4 = Resistor [tolerance=±5% resistance=100 package="1206 [SMD]"]

nets:
  N1: Компонент1.A1, R4.Pin_0
  N2: Компонент1.A4/SDA, LCM1602_IIC1.SDA
  N3: Компонент1.A5/SCL, LCM1602_IIC1.SCL
  N4: Компонент1.D9_PWM, S7.Pin_3
  N5: Компонент1.D10_PWM/SS, LED2.cathode
  N6: Компонент1.D12/MISO, S6.Pin_3
  N7: Компонент1.D13/SCK, LED3.cathode
  GND: Компонент1.GND, VCC2.-, S1.L2, LCM1602_IIC1.GND, DC-DC_5V_to_3V3.GND, SG4.2, S6.Pin_1, S6.Pin_2, S7.Pin_1, S8.Pin_1, S8.Pin_2
  N8: Компонент1.D6_PWM, S8.Pin_3
  N9: Компонент1.D7, LED1.cathode
  VIN: Компонент1.VIN, S1.COM, DC-DC_5V_to_3V3.VIN
  N10: VCC2.+, S1.L1
  VSS: LCD1.VSS, LCM1602_IIC1.VSS
  VDD: LCD1.VDD, LCM1602_IIC1.VDD
  N11: LCD1.V0, LCM1602_IIC1.V0
  N12: LCD1.RS, LCM1602_IIC1.RS
  N13: LCD1.R/W, LCM1602_IIC1.RW
  N14: LCD1.E, LCM1602_IIC1.E
  N15: LCD1.DB0, LCM1602_IIC1.D0
  N16: LCD1.DB1, LCM1602_IIC1.D1
  N17: LCD1.DB2, LCM1602_IIC1.D2
  N18: LCD1.DB3, LCM1602_IIC1.D3
  N19: LCD1.DB4, LCM1602_IIC1.D4
  N20: LCD1.DB5, LCM1602_IIC1.D5
  N21: LCD1.DB6, LCM1602_IIC1.D6
  N22: LCD1.DB7, LCM1602_IIC1.D7
  N23: LCD1.LED+, LCM1602_IIC1.A
  N24: LCD1.LED-, LCM1602_IIC1.K
  N25: LCM1602_IIC1.VCC, DC-DC_5V_to_3V3.VOUT
  N26: SG4.1, R4.Pin_1
  N27: LED1.anode, R1-3.Pin_1
  N28: LED2.anode, R3.Pin_1
  N29: LED3.anode, R1.Pin_1
  N30: R1.Pin_0, R1-3.Pin_0, R3.Pin_0, DC-DC_5V_to_3V3_2.VOUT

custom parts:
  LCM1602 IIC: I2C-Module to use a 1602 or 2004 LCD on with the wire.h libory Serial LCD Modul
  Piezo: Buzzer Spark Fun Electronics SIK for MicroView
